// Logisim project DD_Lab_Circuits.circ as structural Verilog
module RippleCarryAdder_subtractor (
  input  S,
  input  A0,
  input  A1,
  input  A2,
  input  A3,
  input  B0,
  input  B1,
  input  B2,
  input  B3,
  output S0,
  output S1,
  output S2,
  output S3,
  output C_out,
  output Overflow
);

  wire fa_1_c_out, fa_2_c_out, fa_3_c_out, xor_1_out, xor_2_out, xor_3_out, xor_4_out;

  xor xor_1 (xor_1_out, B0, S);
  xor xor_2 (xor_2_out, B1, S);
  xor xor_3 (xor_3_out, B2, S);
  xor xor_4 (xor_4_out, B3, S);
  FA fa_1 (.A(A0), .B(xor_1_out), .C_in(S), .SUM(S0), .C_out(fa_1_c_out));
  FA fa_2 (.A(A1), .B(xor_2_out), .C_in(fa_1_c_out), .SUM(S1), .C_out(fa_2_c_out));
  FA fa_3 (.A(A2), .B(xor_3_out), .C_in(fa_2_c_out), .SUM(S2), .C_out(fa_3_c_out));
  FA fa_4 (.A(A3), .B(xor_4_out), .C_in(fa_3_c_out), .SUM(S3), .C_out(C_out));
  xor xor_5 (Overflow, C_out, fa_3_c_out);
  LED led_1 (.in(Overflow));

  // Notes on the sheet:
  //    A+B or A-B, LED indicates overflow
  //   ID 2018B5A30894 (2+4)
  //   ID 0894   2+4
endmodule

module HA (
  input  A,
  input  B,
  output Sum,
  output C_out
);

  xor xor_1 (Sum, A, B);
  and and_1 (C_out, B, A);
endmodule

module FA (
  input  A,
  input  B,
  input  C_in,
  output SUM,
  output C_out
);

  wire ha_1_c_out, ha_1_sum, ha_2_c_out;

  HA ha_1 (.A(A), .B(B), .Sum(ha_1_sum), .C_out(ha_1_c_out));
  HA ha_2 (.A(ha_1_sum), .B(C_in), .Sum(SUM), .C_out(ha_2_c_out));
  or or_1 (C_out, ha_2_c_out, ha_1_c_out);
endmodule

module RCAdderWithinputoutput (
  input  Add_Or_Subtract,
  input  in_2,
  input  A_LSB,
  input  in_4,
  input  in_5,
  input  in_6,
  input  in_7,
  input  Answer_MSB,
  input  in_9,
  input  in_10,
  input  C_out,
  input  B_LSB,
  input  in_13,
  input  in_14,
  input  Overflow,
  input  Add_Or_Subtract_2,
  input  A_LSB_2,
  input  in_18,
  input  in_19,
  input  in_20,
  input  in_21,
  input  B_MSB,
  input  in_23,
  input  in_24,
  input  C_out_2,
  input  Overflow_2
);

  RippleCarryAdder_subtractor ripplecarryadder_subtractor_1 (
    .A0(A_LSB), .A1(in_4), .A2(in_5), .A3(in_9), .B0(in_10), .B1(in_14), .B2(in_13), .B3(B_LSB),
    .S(Add_Or_Subtract), .S0(in_2), .S1(in_6), .S2(in_7), .S3(Answer_MSB), .C_out(C_out), .Overflow(C_out));
  RippleCarryAdder_subtractor ripplecarryadder_subtractor_2 (
    .A0(A_LSB_2), .A1(in_18), .A2(in_19), .A3(in_20), .B0(in_21), .B1(in_24), .B2(in_23), .B3(B_MSB),
    .S(Add_Or_Subtract_2), .C_out(C_out_2), .Overflow(Overflow_2));  // open: S0, S1, S2, S3

  assign Overflow = C_out;
endmodule

module BCD_addn_and_then_7Seg_display (
  input  A3,
  input  A2,
  input  A1,
  input  A0,
  input  B0,
  input  B3,
  input  B2,
  input  B1,
  output Z0,
  output Z1,
  output Z2,
  output Z3,
  output Overflow,
  output C
);

  wire _4_bit_Adder_c_out, _4_bit_Adder_s0, _4_bit_Adder_s1, _4_bit_Adder_s2, _4_bit_Adder_s3, and_1_out,
       and_2_out, BCD_to_7Seg_a, BCD_to_7Seg_b, BCD_to_7Seg_c, BCD_to_7Seg_d, BCD_to_7Seg_e, BCD_to_7Seg_f,
       BCD_to_7Seg_g, or_1_out;

  BCD_to_7Seg_display BCD_to_7Seg (
    .a(BCD_to_7Seg_a), .b(BCD_to_7Seg_b), .c(BCD_to_7Seg_c), .d(BCD_to_7Seg_d), .e(BCD_to_7Seg_e),
    .f(BCD_to_7Seg_f), .g(BCD_to_7Seg_g), .X3(Z3), .X2(Z2), .X1(Z1), .X0(Z0));
  RippleCarryAdder_subtractor _4_bit_Adder (
    .A0(A0), .A1(A1), .A2(A2), .A3(A3), .B0(B0), .B1(B1), .B2(B2), .B3(B3), .S(1'b0), .S0(_4_bit_Adder_s0),
    .S1(_4_bit_Adder_s1), .S2(_4_bit_Adder_s2), .S3(_4_bit_Adder_s3), .C_out(_4_bit_Adder_c_out),
    .Overflow(Overflow));
  and and_1 (and_1_out, _4_bit_Adder_s3, _4_bit_Adder_s1);
  and and_2 (and_2_out, _4_bit_Adder_s2, _4_bit_Adder_s3);
  or or_1 (or_1_out, and_1_out, and_2_out);
  RippleCarryAdder_subtractor _4_bit_Adder_2 (
    .A0(_4_bit_Adder_s0), .A1(_4_bit_Adder_s1), .A2(_4_bit_Adder_s2), .A3(_4_bit_Adder_s3), .B0(1'b0),
    .B1(C), .B2(C), .B3(1'b0), .S(1'b0), .S0(Z0), .S1(Z1), .S2(Z2), .S3(Z3));  // open: C_out, Overflow
  or or_2 (C, or_1_out, _4_bit_Adder_c_out);
  _7_Segment_Display u_7_segment_display_1 (
    .g(BCD_to_7Seg_g), .f(BCD_to_7Seg_f), .a(BCD_to_7Seg_a), .b(BCD_to_7Seg_b), .e(BCD_to_7Seg_e),
    .d(BCD_to_7Seg_d), .c(BCD_to_7Seg_c));  // open: dp
  _7_Segment_Display u_7_segment_display_2 (.b(C), .c(C));  // open: g, f, a, e, d, dp

  // Other names for the same wires on the sheet: LSB_of_next_BCD_digit = C

  // Notes on the sheet:
  //   ID 0894  A+B=9+4
endmodule

module BCD_to_7Seg_display (
  input  X3,
  input  X2,
  input  X1,
  input  X0,
  output a,
  output b,
  output c,
  output d,
  output e,
  output f,
  output g
);

  wire and_1_out, and_2_out, and_3_out, and_4_out, and_5_out, and_6_out, and_7_out, and_8_out, and_9_out,
       not_1_out, not_2_out, not_3_out;

  not not_1 (not_1_out, X2);
  not not_2 (not_2_out, X0);
  not not_3 (not_3_out, X1);
  and and_1 (and_1_out, X2, X0);
  and and_2 (and_2_out, not_1_out, not_2_out);
  and and_3 (and_3_out, X1, X0);
  and and_4 (and_4_out, not_3_out, not_2_out);
  and and_5 (and_5_out, X1, not_2_out);
  and and_6 (and_6_out, not_1_out, X1);
  and and_7 (and_7_out, X2, not_3_out);
  and and_8 (and_8_out, X2, not_2_out);
  and and_9 (and_9_out, X0, and_7_out);
  or or_1 (a, and_1_out, and_2_out, X3, X1);
  or or_2 (b, and_3_out, not_1_out, and_4_out);
  or or_3 (c, X2, not_3_out, X0);
  or or_4 (d, and_5_out, and_2_out, X3, and_9_out, and_6_out);
  or or_5 (e, and_2_out, and_5_out);
  or or_6 (f, X3, and_4_out, and_8_out, and_7_out);
  or or_7 (g, and_5_out, and_7_out, and_6_out, X3);

  // Notes on the sheet:
  //   I reversed the order of x0 to x4 in representation of this module
endmodule

module Latch (
  input  in_1,
  input  in_2,
  output out_3,
  output out_4
);

  nand nand_1 (out_3, in_1, out_4);
  nand nand_2 (out_4, out_3, in_2);
endmodule
