// Logisim project LAB_1.circ as structural Verilog: 1 circuit, main circuit B1
module B1 (
  input  G0,
  input  G1,
  input  G2,
  input  G3,
  output b0,
  output b1,
  output b2,
  output b3
);

  xor xor_1 (b2, G2, G3);
  xor xor_2 (b1, G1, b2);
  xor xor_3 (b0, G0, b1);

  assign b3 = G3;

  // Notes on the sheet:
  //   MSB
  //   LSB
  //   0894
endmodule
