// Logisim project Lab5_2018B5A30894.circ as structural Verilog: 4 circuits, main circuit 3 to 8 line decoder
module _3_to_8_line_decoder (
  input  B2,
  input  B1,
  input  B0,
  input  ENABLE,
  output Y0,
  output Y1,
  output Y2,
  output Y3,
  output Y4,
  output Y5,
  output Y6,
  output Y7
);

  wire not_1_out, not_2_out, not_3_out;

  not not_1 (not_1_out, B2);
  not not_2 (not_2_out, B1);
  not not_3 (not_3_out, B0);
  nand nand_1 (Y0, not_1_out, not_2_out, not_3_out, ENABLE);
  nand nand_2 (Y1, not_1_out, not_2_out, B0, ENABLE);
  nand nand_3 (Y2, not_1_out, B1, not_3_out, ENABLE);
  nand nand_4 (Y3, not_1_out, B1, B0, ENABLE);
  nand nand_5 (Y4, B2, not_3_out, not_2_out, ENABLE);
  nand nand_6 (Y5, B2, not_2_out, B0, ENABLE);
  nand nand_7 (Y6, B2, B1, not_3_out, ENABLE);
  nand nand_8 (Y7, B2, B1, B0, ENABLE);
endmodule

module _1_to_2_line_decoder (
  input  B0,
  input  ENABLE,
  output A0,
  output A1
);

  wire not_1_out;

  nand nand_1 (A0, B0, ENABLE);
  not not_1 (not_1_out, B0);
  nand nand_2 (A1, not_1_out, ENABLE);
endmodule

module _4_to_16_line_decoder (
  input  B3,
  input  B2,
  input  B1,
  input  B0,
  input  ENABLE,
  output Y0,
  output Y1,
  output Y2,
  output Y3,
  output Y4,
  output Y5,
  output Y6,
  output Y7,
  output Y8,
  output Y9,
  output Y10,
  output Y11,
  output Y12,
  output Y13,
  output Y14,
  output Y15
);

  wire n1_to_2_line_decoder_1_a0, n1_to_2_line_decoder_1_a1;

  _1_to_2_line_decoder u_1_to_2_line_decoder_1 (
    .B0(B3), .ENABLE(ENABLE), .A0(n1_to_2_line_decoder_1_a0), .A1(n1_to_2_line_decoder_1_a1));
  _3_to_8_line_decoder u_3_to_8_line_decoder_1 (
    .B2(B2), .B1(B1), .B0(B0), .ENABLE(n1_to_2_line_decoder_1_a0), .Y0(Y0), .Y1(Y1), .Y2(Y2), .Y3(Y3),
    .Y4(Y4), .Y5(Y5), .Y6(Y6), .Y7(Y7));
  _3_to_8_line_decoder u_3_to_8_line_decoder_2 (
    .B2(B2), .B1(B1), .B0(B0), .ENABLE(n1_to_2_line_decoder_1_a1), .Y0(Y8), .Y1(Y9), .Y2(Y10), .Y3(Y11),
    .Y4(Y12), .Y5(Y13), .Y6(Y14), .Y7(Y15));
endmodule

module BCD_to_Ex3_converter (
  input  B3,
  input  B2,
  input  B1,
  input  B0,
  input  ENABLE,
  output A3,
  output A2,
  output A1,
  output A0
);

  wire n4_to_16_line_decoder_1_y0, n4_to_16_line_decoder_1_y1, n4_to_16_line_decoder_1_y2,
       n4_to_16_line_decoder_1_y3, n4_to_16_line_decoder_1_y4, n4_to_16_line_decoder_1_y5,
       n4_to_16_line_decoder_1_y6, n4_to_16_line_decoder_1_y7, n4_to_16_line_decoder_1_y8,
       n4_to_16_line_decoder_1_y9;

  _4_to_16_line_decoder u_4_to_16_line_decoder_1 (
    .B3(B3), .B2(B2), .B1(B1), .B0(B0), .ENABLE(ENABLE), .Y0(n4_to_16_line_decoder_1_y0),
    .Y1(n4_to_16_line_decoder_1_y1), .Y2(n4_to_16_line_decoder_1_y2), .Y3(n4_to_16_line_decoder_1_y3),
    .Y4(n4_to_16_line_decoder_1_y4), .Y5(n4_to_16_line_decoder_1_y5), .Y6(n4_to_16_line_decoder_1_y6),
    .Y7(n4_to_16_line_decoder_1_y7), .Y8(n4_to_16_line_decoder_1_y8), .Y9(n4_to_16_line_decoder_1_y9));  // open: Y10, Y11, Y12, Y13, Y14, Y15
  and and_1 (A3, n4_to_16_line_decoder_1_y0, n4_to_16_line_decoder_1_y1, n4_to_16_line_decoder_1_y2, n4_to_16_line_decoder_1_y3, n4_to_16_line_decoder_1_y4);
  and and_2 (A2, n4_to_16_line_decoder_1_y0, n4_to_16_line_decoder_1_y5, n4_to_16_line_decoder_1_y6, n4_to_16_line_decoder_1_y7, n4_to_16_line_decoder_1_y8);
  and and_3 (A1, n4_to_16_line_decoder_1_y1, n4_to_16_line_decoder_1_y2, n4_to_16_line_decoder_1_y5, n4_to_16_line_decoder_1_y6, n4_to_16_line_decoder_1_y9);
  and and_4 (A0, n4_to_16_line_decoder_1_y1, n4_to_16_line_decoder_1_y3, n4_to_16_line_decoder_1_y5, n4_to_16_line_decoder_1_y7, n4_to_16_line_decoder_1_y9);

  // Notes on the sheet:
  //   ID:0894
endmodule
