// Logisim project Lab5_AS.circ as structural Verilog: 3 circuits, main circuit 3 to 8 line decoder active low
module _3_to_8_line_decoder_active_low (
  input  w2,
  input  w1,
  input  w0,
  input  ENABLE,
  output Q0,
  output Q1,
  output Q2,
  output Q3,
  output Q4,
  output Q5,
  output Q6,
  output Q7
);

  wire not_1_out, not_2_out, not_3_out;

  not not_1 (not_1_out, w2);
  not not_2 (not_2_out, w1);
  not not_3 (not_3_out, w0);
  nand nand_1 (Q0, not_1_out, not_2_out, not_3_out, ENABLE);
  nand nand_2 (Q1, not_1_out, not_2_out, w0, ENABLE);
  nand nand_3 (Q2, not_1_out, w1, not_3_out, ENABLE);
  nand nand_4 (Q3, not_1_out, w1, w0, ENABLE);
  nand nand_5 (Q4, w2, not_3_out, not_2_out, ENABLE);
  nand nand_6 (Q5, w2, not_2_out, w0, ENABLE);
  nand nand_7 (Q6, w2, w1, not_3_out, ENABLE);
  nand nand_8 (Q7, w2, w1, w0, ENABLE);
endmodule

module _1_2_Decoder_acttive_low (
  input  S,
  input  EN,
  output y0,
  output y1
);

  wire not_1_out, not_2_out;

  not not_1 (not_1_out, S);
  not not_2 (not_2_out, not_1_out);
  nand nand_1 (y1, not_2_out, EN);
  nand nand_2 (y0, not_1_out, EN);
endmodule

module _4_16_Decoder_active_low (
  input  W0,
  input  W1,
  input  W2,
  input  W3,
  input  Enable,
  output y0,
  output y1,
  output y2,
  output y3,
  output y4,
  output y5,
  output y6,
  output y7,
  output y8,
  output y9,
  output y10,
  output y11,
  output y12,
  output y13,
  output y14,
  output y15
);

  wire n1_2_decoder_acttive_low_1_y0, n1_2_decoder_acttive_low_1_y1;

  _1_2_Decoder_acttive_low u_1_2_decoder_acttive_low_1 (
    .S(W3), .EN(Enable), .y0(n1_2_decoder_acttive_low_1_y0), .y1(n1_2_decoder_acttive_low_1_y1));
  _3_to_8_line_decoder_active_low u_3_to_8_line_decoder_active_low_1 (
    .w2(W2), .w1(W1), .w0(W0), .ENABLE(n1_2_decoder_acttive_low_1_y1), .Q0(y0), .Q1(y1), .Q2(y2), .Q3(y3),
    .Q4(y4), .Q5(y5), .Q6(y6), .Q7(y7));
  _3_to_8_line_decoder_active_low u_3_to_8_line_decoder_active_low_2 (
    .w2(W2), .w1(W1), .w0(W0), .ENABLE(n1_2_decoder_acttive_low_1_y0), .Q0(y8), .Q1(y9), .Q2(y10), .Q3(y11),
    .Q4(y12), .Q5(y13), .Q6(y14), .Q7(y15));
endmodule
