// Logisim project Lab6.circ as structural Verilog: 5 circuits, main circuit main
module main (
  input  wo__select_lines,
  input  w1,
  input  I0,
  input  I1,
  input  I2,
  input  I3,
  input  ENABLE,
  output Output
);

  wire and_1_out, and_2_out, and_3_out, and_4_out, not_1_out, not_2_out;

  not not_1 (not_1_out, wo__select_lines);
  not not_2 (not_2_out, w1);
  and and_1 (and_1_out, not_1_out, I0, not_2_out, ENABLE);
  and and_2 (and_2_out, wo__select_lines, not_2_out, I1, ENABLE);
  and and_3 (and_3_out, w1, I2, not_1_out, ENABLE);
  and and_4 (and_4_out, I3, wo__select_lines, w1, ENABLE);
  or or_1 (Output, and_1_out, and_2_out, and_3_out, and_4_out);

  // Notes on the sheet:
  //   LSB
  //   Selector Switch
endmodule

module _4_1_Multiplexer (
  input  wo__select_lines,
  input  w1,
  input  I0,
  input  I1,
  input  I2,
  input  I3,
  input  ENABLE,
  output Output
);

  wire and_1_out, and_2_out, and_3_out, and_4_out, not_1_out, not_2_out;

  not not_1 (not_1_out, wo__select_lines);
  not not_2 (not_2_out, w1);
  and and_1 (and_1_out, not_1_out, I0, not_2_out, ENABLE);
  and and_2 (and_2_out, wo__select_lines, not_2_out, I1, ENABLE);
  and and_3 (and_3_out, w1, I2, not_1_out, ENABLE);
  and and_4 (and_4_out, I3, wo__select_lines, w1, ENABLE);
  or or_1 (Output, and_1_out, and_2_out, and_3_out, and_4_out);

  // Notes on the sheet:
  //   LSB
endmodule

module _8_1_Mux (
  input  A__MSB,
  input  B,
  input  C__LSB,
  input  I0,
  input  I1,
  input  I2,
  input  I3,
  input  I4,
  input  I5,
  input  I6,
  input  I7,
  input  En,
  output Output
);

  wire n4_1_multiplexer_1_output, n4_1_multiplexer_2_output;

  _4_1_Multiplexer u_4_1_multiplexer_1 (
    .wo__select_lines(C__LSB), .w1(B), .I0(I0), .I1(I1), .I2(I2), .I3(I3), .ENABLE(En),
    .Output(n4_1_multiplexer_1_output));
  _4_1_Multiplexer u_4_1_multiplexer_2 (
    .wo__select_lines(C__LSB), .w1(B), .I0(I4), .I1(I5), .I2(I6), .I3(I7), .ENABLE(En),
    .Output(n4_1_multiplexer_2_output));
  _4_1_Multiplexer u_4_1_multiplexer_3 (
    .wo__select_lines(A__MSB), .w1(1'b1), .I0(1'b0), .I1(1'b0), .I2(n4_1_multiplexer_1_output),
    .I3(n4_1_multiplexer_2_output), .ENABLE(En), .Output(Output));

  // Notes on the sheet:
  //   ID:0894
endmodule

module function_real___4_1 (
  input  D,
  input  C,
  input  B,
  input  En,
  input  A,
  output Y
);

  wire and_1_out, not_1_out, or_1_out;

  not not_1 (not_1_out, D);
  and and_1 (and_1_out, D, A);
  or or_1 (or_1_out, not_1_out, A);
  _4_1_Multiplexer u_4_1_multiplexer_1 (
    .wo__select_lines(C), .w1(B), .I0(or_1_out), .I1(1'b1), .I2(1'b1), .I3(and_1_out), .ENABLE(En), .Output(Y));

  // Notes on the sheet:
  //   ID:0894
endmodule

module Func__real__8_1 (
  input  A,
  input  B,
  input  C,
  input  D,
  input  En,
  output Y
);

  _8_1_Mux u_8_1_mux_1 (
    .A__MSB(B), .B(C), .C__LSB(D), .I0(1'b1), .I1(A), .I2(1'b1), .I3(1'b1), .I4(1'b1), .I5(1'b1), .I6(1'b0),
    .I7(A), .En(En), .Output(Y));
endmodule
