// Logisim project Multiplexer Demultiplexer_AS.circ as structural Verilog
module _4_1_Multiplexer (
  input  S0,
  input  S1,
  input  I0,
  input  I1,
  input  I2,
  input  I3,
  input  ENABLE,
  output yo,
  output y1,
  output Output,
  output y2,
  output y3
);

  wire not_1_out, not_2_out;

  not not_1 (not_1_out, S0);
  not not_2 (not_2_out, S1);
  and and_1 (yo, not_1_out, I0, not_2_out, ENABLE);
  and and_2 (y1, S0, not_2_out, I1, ENABLE);
  and and_3 (y2, S1, I2, not_1_out, ENABLE);
  and and_4 (y3, I3, S0, S1, ENABLE);
  or or_1 (Output, yo, y1, y2, y3);

  // Notes on the sheet:
  //   LSB
  //   Select Line
  //   Universal func generator
  //   Majority circuit
  //   Universal Function generator
  //   Parallel to serial data
  //   Logic Function Genereator
  //   Selector Switch
endmodule

module _2_1_mux (
  input  S0,
  input  I0,
  input  I1,
  input  EN,
  output Output
);

  wire and_1_out, and_2_out, not_1_out;

  not not_1 (not_1_out, S0);
  and and_1 (and_1_out, not_1_out, EN, I0);
  and and_2 (and_2_out, S0, EN, I1);
  or or_1 (Output, and_1_out, and_2_out);

  // Notes on the sheet:
  //   S0'*I0+S0*I1
endmodule

module _8_1_mux (
  input  C__LSB,
  input  B,
  input  A__MSB,
  input  I0,
  input  I1,
  input  I2,
  input  I3,
  input  I4,
  input  I5,
  input  I6,
  input  I7,
  output Output
);

  wire n4_1_multiplexer_1_output, n4_1_multiplexer_2_output, not_1_out;

  not not_1 (not_1_out, A__MSB);
  _4_1_Multiplexer u_4_1_multiplexer_1 (
    .S0(C__LSB), .S1(B), .I0(I0), .I1(I1), .I2(I2), .I3(I3), .ENABLE(not_1_out),
    .Output(n4_1_multiplexer_1_output));  // open: yo, y1, y2, y3
  _4_1_Multiplexer u_4_1_multiplexer_2 (
    .S0(C__LSB), .S1(B), .I0(I4), .I1(I5), .I2(I6), .I3(I7), .ENABLE(A__MSB),
    .Output(n4_1_multiplexer_2_output));  // open: yo, y1, y2, y3
  or or_1 (Output, n4_1_multiplexer_1_output, n4_1_multiplexer_2_output);
endmodule

module FASTER_8_1_MUX_using_only_mux (
  input  A__MSB,
  input  B,
  input  C__LSB,
  input  I0,
  input  I1,
  input  I2,
  input  I3,
  input  I4,
  input  I5,
  input  I6,
  input  I7,
  input  En,
  output Output
);

  wire n4_1_multiplexer_1_output, n4_1_multiplexer_2_output;

  _4_1_Multiplexer u_4_1_multiplexer_1 (
    .S0(C__LSB), .S1(B), .I0(I0), .I1(I1), .I2(I2), .I3(I3), .ENABLE(En), .Output(n4_1_multiplexer_1_output));  // open: yo, y1, y2, y3
  _4_1_Multiplexer u_4_1_multiplexer_2 (
    .S0(C__LSB), .S1(B), .I0(I4), .I1(I5), .I2(I6), .I3(I7), .ENABLE(En), .Output(n4_1_multiplexer_2_output));  // open: yo, y1, y2, y3
  _2_1_mux u_2_1_mux_1 (
    .S0(A__MSB), .I0(n4_1_multiplexer_1_output), .I1(n4_1_multiplexer_2_output), .EN(En), .Output(Output));
endmodule

module Multiplexer_to_Demultiplexer (
  input  En,
  input  d1,
  input  d0,
  input  S0,
  input  S1,
  input  I0,
  input  I1,
  input  I2,
  input  I3,
  input  En_2,
  output O0,
  output O1,
  output O2,
  output O3
);

  wire n4_1_multiplexer_1_output, not_1_out, not_2_out;

  _4_1_Multiplexer u_4_1_multiplexer_1 (
    .S0(S0), .S1(S1), .I0(I0), .I1(I1), .I2(I2), .I3(I3), .ENABLE(En_2), .Output(n4_1_multiplexer_1_output));  // open: yo, y1, y2, y3
  not not_1 (not_1_out, d1);
  not not_2 (not_2_out, d0);
  and and_1 (O0, not_2_out, not_1_out, n4_1_multiplexer_1_output, En);
  and and_2 (O1, not_1_out, d0, n4_1_multiplexer_1_output, En);
  and and_3 (O2, not_2_out, d1, n4_1_multiplexer_1_output, En);
  and and_4 (O3, d1, d0, n4_1_multiplexer_1_output, En);

  // Notes on the sheet:
  //   MSB
  //   LSB
  //   00,01,10,11
  //   00,01,10,11
  //   I3-o3,i2-o2-i1-i1-i0-o0
  //   1:n
endmodule

module _1_4_Demultiplexer (
  input  En,
  input  d1,
  input  d0,
  input  DATA,
  output Y0,
  output Y1,
  output Y2,
  output Y3
);

  wire not_1_out, not_2_out;

  not not_1 (not_1_out, d1);
  not not_2 (not_2_out, d0);
  and and_1 (Y0, not_2_out, not_1_out, DATA, En);
  and and_2 (Y1, not_1_out, d0, DATA, En);
  and and_3 (Y2, not_2_out, d1, DATA, En);
  and and_4 (Y3, d1, d0, DATA, En);

  // Notes on the sheet:
  //   serial to parallel
  //   Deselector
endmodule

module OR_Gate_from_mux (
  input  A,
  input  B,
  input  in_3,
  input  A_2,
  input  _1,
  input  _1_2,
  input  _1_3,
  input  B_2,
  input  _1_4,
  input  in_10,
  input  in_11,
  output out_12,
  output out_13
);

  _4_1_Multiplexer u_4_1_multiplexer_1 (
    .S0(A), .S1(B), .I0(in_3), .I1(_1), .I2(_1_2), .I3(_1_3), .ENABLE(in_10), .Output(out_12));  // open: yo, y1, y2, y3
  _2_1_mux u_2_1_mux_1 (.S0(A_2), .I0(B_2), .I1(_1_4), .EN(in_11), .Output(out_13));
endmodule

module AND_Gate_from_Mux (
  input  A,
  input  A_2,
  input  B,
  input  _0,
  input  B_2,
  input  in_6,
  input  in_7,
  input  in_8,
  input  _1,
  input  in_10,
  input  in_11,
  output out_12,
  output out_13
);

  _4_1_Multiplexer u_4_1_multiplexer_1 (
    .S0(A), .S1(B), .I0(in_6), .I1(in_7), .I2(in_8), .I3(_1), .ENABLE(in_11), .Output(out_13));  // open: yo, y1, y2, y3
  _2_1_mux u_2_1_mux_1 (.S0(A_2), .I0(_0), .I1(B_2), .EN(in_10), .Output(out_12));
endmodule

module XNOR_using_mux (
  input  A,
  input  B,
  input  A_2,
  input  _1,
  input  in_5,
  input  in_6,
  input  B_BAR,
  input  _1_2,
  input  B_2,
  input  in_10,
  input  in_11,
  output out_12,
  output out_13
);

  _4_1_Multiplexer u_4_1_multiplexer_1 (
    .S0(A), .S1(B), .I0(_1), .I1(in_5), .I2(in_6), .I3(_1_2), .ENABLE(in_10), .Output(out_12));  // open: yo, y1, y2, y3
  _2_1_mux u_2_1_mux_1 (.S0(A_2), .I0(B_BAR), .I1(B_2), .EN(in_11), .Output(out_13));
endmodule

module NOT_Gate_using_mux (
  input  A,
  input  _1,
  input  _0,
  input  en,
  output out_5
);

  _2_1_mux u_2_1_mux_1 (.S0(A), .I0(_1), .I1(_0), .EN(en), .Output(out_5));
endmodule
