// Logisim project RippleCarryAdder_Substractor2.circ as structural Verilog: 3 circuits, main circuit main
module main (
  input  S,
  input  A0,
  input  B0,
  input  A1,
  input  B1,
  input  A2,
  input  B2,
  input  A3,
  input  B3,
  output S0,
  output S1,
  output S2,
  output S3,
  output C_out
);

  wire fa_1_c_out, fa_2_c_out, fa_3_c_out, xor_1_out, xor_2_out, xor_3_out, xor_4_out, xor_5_out;

  xor xor_1 (xor_1_out, B0, S);
  xor xor_2 (xor_2_out, B1, S);
  xor xor_3 (xor_3_out, B2, S);
  xor xor_4 (xor_4_out, B3, S);
  FA fa_1 (.A(A0), .B(xor_1_out), .C_in(S), .SUM(S0), .C_out(fa_1_c_out));
  FA fa_2 (.A(A1), .B(xor_2_out), .C_in(fa_1_c_out), .SUM(S1), .C_out(fa_2_c_out));
  FA fa_3 (.A(A2), .B(xor_3_out), .C_in(fa_2_c_out), .SUM(S2), .C_out(fa_3_c_out));
  FA fa_4 (.A(A3), .B(xor_4_out), .C_in(fa_3_c_out), .SUM(S3), .C_out(C_out));
  xor xor_5 (xor_5_out, C_out, fa_3_c_out);
  LED led_1 (.in(xor_5_out));

  // Notes on the sheet:
  //    A+B or A-B, LED indicates overflow
  //   ID 2018B5A30894 (2+4)
  //   ID 0894   2+4
endmodule

module HA (
  input  A,
  input  B,
  output Sum,
  output C_out
);

  xor xor_1 (Sum, A, B);
  and and_1 (C_out, B, A);
endmodule

module FA (
  input  A,
  input  B,
  input  C_in,
  output SUM,
  output C_out
);

  wire ha_1_c_out, ha_1_sum, ha_2_c_out;

  HA ha_1 (.A(A), .B(B), .Sum(ha_1_sum), .C_out(ha_1_c_out));
  HA ha_2 (.A(ha_1_sum), .B(C_in), .Sum(SUM), .C_out(ha_2_c_out));
  or or_1 (C_out, ha_2_c_out, ha_1_c_out);
endmodule
