// Logisim project lab4.circ as structural Verilog: 7 circuits, main circuit JK Flip Flop
module JK_Flip_Flop (
  input  Preset,
  input  J,
  input  K,
  input  Clear,
  output Q,
  output Q_bar
);

  wire Clock_out, nand_1_out, nand_2_out, nand_3_out, nand_4_out, nand_5_out, nand_6_out, not_1_out;

  Clock Clock (.out(Clock_out));
  nand nand_1 (nand_1_out, Q_bar, J, Clock_out);
  nand nand_2 (nand_2_out, Clock_out, K, Q);
  nand nand_3 (nand_3_out, Preset, nand_1_out, nand_4_out);
  nand nand_4 (nand_4_out, nand_3_out, nand_2_out, Clear);
  not not_1 (not_1_out, Clock_out);
  nand nand_5 (nand_5_out, nand_3_out, not_1_out);
  nand nand_6 (nand_6_out, not_1_out, nand_4_out);
  nand nand_7 (Q, Preset, nand_5_out, Q_bar);
  nand nand_8 (Q_bar, Q, nand_6_out, Clear);

  // Notes on the sheet:
  //   Master slave JK flip flop
  //   ID:0894
endmodule

module Delay_Flip_Flop (
  input  Preset,
  input  D,
  input  Clear,
  output Q,
  output Q_bar
);

  wire Clock_out, nand_1_out, nand_2_out, nand_3_out, nand_4_out, nand_5_out, nand_6_out, not_1_out,
       not_2_out;

  not not_1 (not_1_out, D);
  Clock Clock (.out(Clock_out));
  nand nand_1 (nand_1_out, Q_bar, D, Clock_out);
  nand nand_2 (nand_2_out, Clock_out, not_1_out, Q);
  nand nand_3 (nand_3_out, Preset, nand_1_out, nand_4_out);
  nand nand_4 (nand_4_out, nand_3_out, nand_2_out, Clear);
  not not_2 (not_2_out, Clock_out);
  nand nand_5 (nand_5_out, nand_3_out, not_2_out);
  nand nand_6 (nand_6_out, not_2_out, nand_4_out);
  nand nand_7 (Q, Preset, nand_5_out, Q_bar);
  nand nand_8 (Q_bar, Q, nand_6_out, Clear);

  // Notes on the sheet:
  //   Delay Flip Flop
endmodule

module Toggle_Flip_Flop (
  input  Preset,
  input  T,
  input  Clear,
  output Q,
  output Q_bar
);

  wire Clock_out, nand_1_out, nand_2_out, nand_3_out, nand_4_out, nand_5_out, nand_6_out, not_1_out;

  Clock Clock (.out(Clock_out));
  nand nand_1 (nand_1_out, Q_bar, T, Clock_out);
  nand nand_2 (nand_2_out, Clock_out, T, Q);
  nand nand_3 (nand_3_out, Preset, nand_1_out, nand_4_out);
  nand nand_4 (nand_4_out, nand_3_out, nand_2_out, Clear);
  not not_1 (not_1_out, Clock_out);
  nand nand_5 (nand_5_out, nand_3_out, not_1_out);
  nand nand_6 (nand_6_out, not_1_out, nand_4_out);
  nand nand_7 (Q, Preset, nand_5_out, Q_bar);
  nand nand_8 (Q_bar, Q, nand_6_out, Clear);

  // Notes on the sheet:
  //   Toggle Flip Flop
endmodule

module JK_using_D (
  input  Preset,
  input  J,
  input  K,
  input  Clear,
  output Q,
  output Q_bar
);

  wire and_1_out, and_2_out, not_1_out, or_1_out;

  not not_1 (not_1_out, K);
  and and_1 (and_1_out, Q_bar, J);
  and and_2 (and_2_out, not_1_out, Q);
  or or_1 (or_1_out, and_1_out, and_2_out);
  Delay_Flip_Flop delay_flip_flop_1 (.D(or_1_out), .Preset(Preset), .Clear(Clear), .Q(Q), .Q_bar(Q_bar));

  // Notes on the sheet:
  //   JK using D Flip Flop
endmodule

module JK_using_T (
  input  Preset,
  input  J,
  input  K,
  input  Clear,
  output Q,
  output Q_bar
);

  wire and_1_out, and_2_out, or_1_out;

  and and_1 (and_1_out, Q_bar, J);
  or or_1 (or_1_out, and_1_out, and_2_out);
  and and_2 (and_2_out, K, Q);
  Toggle_Flip_Flop toggle_flip_flop_1 (.T(or_1_out), .Preset(Preset), .Clear(Clear), .Q(Q), .Q_bar(Q_bar));

  // Notes on the sheet:
  //   JK using T Flip Flop
endmodule

module Toggle_Using_JK (
  input  Preset,
  input  Toggle,
  input  Clear,
  output Q,
  output Q_bar
);

  JK_Flip_Flop jk_flip_flop_1 (.J(Toggle), .K(Toggle), .Preset(Preset), .Clear(Clear), .Q(Q), .Q_bar(Q_bar));

  // Notes on the sheet:
  //   T Flip Flop using JK Flip Flop
endmodule

module Delay_Using_JK (
  input  Preset,
  input  Delay,
  input  Clear,
  output Q,
  output Q_bar
);

  wire not_1_out;

  JK_Flip_Flop jk_flip_flop_1 (.J(Delay), .K(not_1_out), .Preset(Preset), .Clear(Clear), .Q(Q), .Q_bar(Q_bar));
  not not_1 (not_1_out, Delay);

  // Notes on the sheet:
  //   D Flip Flop using JK Flip Flop
endmodule
