// Logisim project lab_1_2.circ as structural Verilog: 1 circuit, main circuit main
module main (
  input  g3,
  input  g2,
  input  g1,
  input  g0,
  output b3,
  output b2,
  output b1,
  output b0
);

  wire and_1_out, and_2_out, and_3_out, and_4_out, and_5_out, and_6_out, not_1_out, not_2_out, not_3_out,
       not_4_out, not_5_out, not_6_out;

  not not_1 (not_1_out, g2);
  not not_2 (not_2_out, g3);
  not not_3 (not_3_out, g1);
  not not_4 (not_4_out, g0);
  and and_1 (and_1_out, g3, not_1_out);
  and and_2 (and_2_out, not_2_out, g2);
  and and_3 (and_3_out, b2, not_3_out);
  not not_5 (not_5_out, b2);
  and and_4 (and_4_out, not_5_out, g1);
  not not_6 (not_6_out, b1);
  and and_5 (and_5_out, b1, not_4_out);
  and and_6 (and_6_out, not_6_out, g0);
  or or_1 (b2, and_1_out, and_2_out);
  or or_2 (b1, and_3_out, and_4_out);
  or or_3 (b0, and_5_out, and_6_out);

  assign b3 = g3;

  // Notes on the sheet:
  //   0894
endmodule
